# Fritzing sketch circuit-diagram (saved by Fritzing 0.8.7b)

parts:
  Raspberry_Pi_Zero1 = Raspberry Pi Zero
  S2 = Pushbutton [package="[THT]"]
  R1 = Resistor [package="2010 [SMD]"]

nets:
  N1: Raspberry_Pi_Zero1.3v3, R1.Pin_0
  N2: Raspberry_Pi_Zero1.GIPO17, S2.Pin_1, S2.Pin_2
  N3: S2.Pin_3, S2.Pin_4, R1.Pin_1
